// Logisim project digital clock.circ as structural Verilog: 14 circuits, main circuit main
module main (
  input  in_1,
  input  in_2,
  input  in_3,
  input  in_4,
  input  in_5,
  input  in_6,
  input  in_7,
  input  in_8
);

  wire clock_1_out, hourcombination_1_a, hourcombination_1_a_3, hourcombination_1_b_2, hourcombination_1_b_3,
       hourcombination_1_c_2, hourcombination_1_c_3, hourcombination_1_d_2, hourcombination_1_d_3,
       hourcombination_1_e, hourcombination_1_e_2, hourcombination_1_f, hourcombination_1_f_2,
       hourcombination_1_g, hourcombination_1_g_2, minmutesclock_1_a_2, minmutesclock_1_a_3,
       minmutesclock_1_b_3, minmutesclock_1_b_4, minmutesclock_1_c_3, minmutesclock_1_c_4,
       minmutesclock_1_d_2, minmutesclock_1_d_3, minmutesclock_1_e, minmutesclock_1_e_2, minmutesclock_1_f,
       minmutesclock_1_f_2, minmutesclock_1_g, minmutesclock_1_g_2, minmutesclock_1_tri, minmutesclock_2_a_2,
       minmutesclock_2_a_3, minmutesclock_2_b_3, minmutesclock_2_b_4, minmutesclock_2_c_3,
       minmutesclock_2_c_4, minmutesclock_2_d_2, minmutesclock_2_d_3, minmutesclock_2_e, minmutesclock_2_e_2,
       minmutesclock_2_f, minmutesclock_2_f_2, minmutesclock_2_g, minmutesclock_2_g_2, minmutesclock_2_tri;

  _7_Segment_Display u_7_segment_display_1 (
    .g(hourcombination_1_g), .f(hourcombination_1_f), .a(hourcombination_1_a), .b(hourcombination_1_b_2),
    .e(hourcombination_1_e), .d(hourcombination_1_d_2), .c(hourcombination_1_c_2));  // open: dp
  _7_Segment_Display u_7_segment_display_2 (
    .g(hourcombination_1_g_2), .f(hourcombination_1_f_2), .a(hourcombination_1_a_3),
    .b(hourcombination_1_b_3), .e(hourcombination_1_e_2), .d(hourcombination_1_d_3), .c(hourcombination_1_c_3));  // open: dp
  hourcombination hourcombination_1 (
    ._10in(in_5), .clk(minmutesclock_1_tri), ._2in(in_5), ._10pre(in_1), ._2pre(in_1),
    .G(hourcombination_1_g), .F(hourcombination_1_f), .g_2(hourcombination_1_g_2),
    .f_2(hourcombination_1_f_2), .e_2(hourcombination_1_e_2), .A(hourcombination_1_a),
    .B_2(hourcombination_1_b_2), .C_2(hourcombination_1_c_2), .D_2(hourcombination_1_d_2),
    .E(hourcombination_1_e), .a_3(hourcombination_1_a_3), .b_3(hourcombination_1_b_3),
    .c_3(hourcombination_1_c_3), .d_3(hourcombination_1_d_3));  // open: out_13, D, C, B, A_2
  _7_Segment_Display u_7_segment_display_3 (
    .g(minmutesclock_1_g_2), .f(minmutesclock_1_f_2), .a(minmutesclock_1_a_2), .b(minmutesclock_1_b_4),
    .e(minmutesclock_1_e_2), .d(minmutesclock_1_d_3), .c(minmutesclock_1_c_4));  // open: dp
  _7_Segment_Display u_7_segment_display_4 (
    .g(minmutesclock_1_g), .f(minmutesclock_1_f), .a(minmutesclock_1_a_3), .b(minmutesclock_1_b_3),
    .e(minmutesclock_1_e), .d(minmutesclock_1_d_2), .c(minmutesclock_1_c_3));  // open: dp
  MINMUTESCLOCK minmutesclock_1 (
    ._10in(in_3), ._0in(in_8), ._6in(in_3), .clk(minmutesclock_2_tri), ._10pre(in_6), ._6pre(in_6),
    .A_2(minmutesclock_1_a_2), .\tri (minmutesclock_1_tri), .a_3(minmutesclock_1_a_3),
    .b_3(minmutesclock_1_b_3), .c_3(minmutesclock_1_c_3), .B_4(minmutesclock_1_b_4),
    .d_2(minmutesclock_1_d_2), .C_4(minmutesclock_1_c_4), .e(minmutesclock_1_e), .D_3(minmutesclock_1_d_3),
    .f(minmutesclock_1_f), .E_2(minmutesclock_1_e_2), .g(minmutesclock_1_g), .F_2(minmutesclock_1_f_2),
    .G_2(minmutesclock_1_g_2));  // open: C_2, B_2, D, C, B, A
  _7_Segment_Display u_7_segment_display_5 (
    .g(minmutesclock_2_g_2), .f(minmutesclock_2_f_2), .a(minmutesclock_2_a_2), .b(minmutesclock_2_b_4),
    .e(minmutesclock_2_e_2), .d(minmutesclock_2_d_3), .c(minmutesclock_2_c_4));  // open: dp
  _7_Segment_Display u_7_segment_display_6 (
    .g(minmutesclock_2_g), .f(minmutesclock_2_f), .a(minmutesclock_2_a_3), .b(minmutesclock_2_b_3),
    .e(minmutesclock_2_e), .d(minmutesclock_2_d_2), .c(minmutesclock_2_c_3));  // open: dp
  Clock clock_1 (.out(clock_1_out));
  MINMUTESCLOCK minmutesclock_2 (
    ._10in(in_2), ._0in(in_7), ._6in(in_2), .clk(clock_1_out), ._10pre(in_4), ._6pre(in_4),
    .A_2(minmutesclock_2_a_2), .\tri (minmutesclock_2_tri), .a_3(minmutesclock_2_a_3),
    .b_3(minmutesclock_2_b_3), .c_3(minmutesclock_2_c_3), .B_4(minmutesclock_2_b_4),
    .d_2(minmutesclock_2_d_2), .C_4(minmutesclock_2_c_4), .e(minmutesclock_2_e), .D_3(minmutesclock_2_d_3),
    .f(minmutesclock_2_f), .E_2(minmutesclock_2_e_2), .g(minmutesclock_2_g), .F_2(minmutesclock_2_f_2),
    .G_2(minmutesclock_2_g_2));  // open: C_2, B_2, D, C, B, A

  // Notes on the sheet:
  //   HOUR
  //   MINUTE
  //   SECOND
  //         2107008
  //   2107007
endmodule

module _7segment (
  input  w,
  input  x,
  input  y,
  input  z,
  output a,
  output b,
  output c,
  output d,
  output e,
  output f,
  output g
);

  wire and_1_out, and_2_out, and_3_out, and_4_out, and_5_out, and_6_out, and_7_out, and_8_out, and_9_out,
       and_10_out, and_11_out, and_12_out, and_13_out, and_14_out, and_15_out, and_16_out, and_17_out,
       and_18_out, and_19_out, and_20_out, and_21_out, and_22_out, and_23_out, and_24_out, and_25_out,
       and_26_out, and_27_out, and_28_out, and_29_out, and_30_out, and_31_out, and_32_out, and_33_out,
       and_34_out, and_35_out, and_36_out, and_37_out, and_38_out, and_39_out, and_40_out, and_41_out,
       and_42_out, and_43_out, and_44_out, and_45_out, and_46_out, not_1_out, not_2_out, not_3_out,
       not_4_out, not_5_out, not_6_out, not_7_out, not_8_out, not_9_out, not_10_out, not_11_out, not_12_out,
       not_13_out, not_14_out, not_15_out, not_16_out, not_17_out, not_18_out, not_19_out, not_20_out,
       not_21_out, not_22_out, not_23_out, not_24_out, not_25_out, not_26_out, not_27_out, not_28_out,
       not_29_out, not_30_out, not_31_out, not_32_out, not_33_out, not_34_out, not_35_out, not_36_out,
       not_37_out, not_38_out, not_39_out, not_40_out, not_41_out, not_42_out, not_43_out, or_1_out,
       or_2_out, or_3_out, or_4_out, or_5_out, or_6_out, or_7_out, or_8_out, or_9_out, or_10_out, or_12_out,
       or_13_out, or_14_out, or_15_out, or_16_out, or_17_out, or_18_out, or_20_out, or_21_out, or_22_out,
       or_23_out;

  not not_1 (not_1_out, x);
  not not_2 (not_2_out, z);
  not not_3 (not_3_out, w);
  not not_4 (not_4_out, w);
  and and_1 (and_1_out, w, not_5_out);
  not not_5 (not_5_out, x);
  not not_6 (not_6_out, y);
  not not_7 (not_7_out, w);
  not not_8 (not_8_out, x);
  not not_9 (not_9_out, w);
  and and_2 (and_2_out, not_9_out, not_10_out);
  not not_10 (not_10_out, y);
  not not_11 (not_11_out, z);
  not not_12 (not_12_out, w);
  not not_13 (not_13_out, y);
  not not_14 (not_14_out, w);
  and and_3 (and_3_out, not_14_out, not_15_out);
  not not_15 (not_15_out, y);
  not not_16 (not_16_out, w);
  and and_4 (and_4_out, not_16_out, z);
  not not_17 (not_17_out, y);
  not not_18 (not_18_out, w);
  not not_19 (not_19_out, x);
  not not_20 (not_20_out, w);
  and and_5 (and_5_out, not_20_out, not_21_out);
  not not_21 (not_21_out, x);
  not not_22 (not_22_out, z);
  not not_23 (not_23_out, x);
  and and_6 (and_6_out, not_23_out, y);
  not not_24 (not_24_out, y);
  not not_25 (not_25_out, x);
  and and_7 (and_7_out, not_25_out, not_26_out);
  not not_26 (not_26_out, z);
  and and_8 (and_8_out, y, not_27_out);
  not not_27 (not_27_out, z);
  and and_9 (and_9_out, w, y);
  and and_10 (and_10_out, w, x);
  not not_28 (not_28_out, y);
  not not_29 (not_29_out, z);
  not not_30 (not_30_out, w);
  and and_11 (and_11_out, not_30_out, x);
  not not_31 (not_31_out, y);
  not not_32 (not_32_out, x);
  and and_12 (and_12_out, not_32_out, y);
  and and_13 (and_13_out, y, not_33_out);
  not not_33 (not_33_out, z);
  not not_34 (not_34_out, w);
  and and_14 (and_14_out, not_34_out, x);
  not not_35 (not_35_out, y);
  not not_36 (not_36_out, x);
  and and_15 (and_15_out, not_1_out, not_2_out);
  and and_16 (and_16_out, not_3_out, y);
  and and_17 (and_17_out, not_4_out, x);
  and and_18 (and_18_out, x, y);
  and and_19 (and_19_out, and_1_out, not_6_out);
  not not_37 (not_37_out, z);
  and and_20 (and_20_out, not_7_out, not_8_out);
  and and_21 (and_21_out, and_2_out, not_11_out);
  not not_38 (not_38_out, x);
  not not_39 (not_39_out, z);
  and and_22 (and_22_out, not_12_out, y);
  and and_23 (and_23_out, w, not_13_out);
  or or_1 (or_1_out, and_3_out, and_4_out);
  and and_24 (and_24_out, not_17_out, z);
  and and_25 (and_25_out, not_18_out, x);
  and and_26 (and_26_out, w, not_19_out);
  and and_27 (and_27_out, and_5_out, not_22_out);
  and and_28 (and_28_out, and_6_out, z);
  and and_29 (and_29_out, x, not_24_out);
  and and_30 (and_30_out, x, y);
  not not_40 (not_40_out, z);
  not not_41 (not_41_out, y);
  or or_2 (or_2_out, and_7_out, and_8_out);
  or or_3 (or_3_out, and_9_out, and_10_out);
  and and_31 (and_31_out, not_28_out, not_29_out);
  and and_32 (and_32_out, and_11_out, not_31_out);
  not not_42 (not_42_out, z);
  not not_43 (not_43_out, x);
  or or_4 (or_4_out, and_12_out, and_13_out);
  and and_33 (and_33_out, and_14_out, not_35_out);
  and and_34 (and_34_out, w, not_36_out);
  and and_35 (and_35_out, w, z);
  or or_5 (or_5_out, and_15_out, and_16_out);
  and and_36 (and_36_out, and_17_out, z);
  or or_6 (or_6_out, and_18_out, and_19_out);
  and and_37 (and_37_out, w, not_37_out);
  or or_7 (or_7_out, and_20_out, and_21_out);
  and and_38 (and_38_out, not_38_out, not_39_out);
  and and_39 (and_39_out, and_22_out, z);
  and and_40 (and_40_out, and_23_out, z);
  or or_8 (or_8_out, or_1_out, and_24_out);
  or or_9 (or_9_out, and_25_out, and_26_out);
  or or_10 (or_10_out, and_27_out, and_28_out);
  and and_41 (and_41_out, and_29_out, z);
  and and_42 (and_42_out, and_30_out, not_40_out);
  and and_43 (and_43_out, w, not_41_out);
  or or_11 (e, or_2_out, or_3_out);
  or or_12 (or_12_out, and_31_out, and_32_out);
  and and_44 (and_44_out, x, not_42_out);
  and and_45 (and_45_out, w, not_43_out);
  and and_46 (and_46_out, w, y);
  or or_13 (or_13_out, or_4_out, and_33_out);
  or or_14 (or_14_out, and_34_out, and_35_out);
  or or_15 (or_15_out, or_5_out, and_36_out);
  or or_16 (or_16_out, or_6_out, and_37_out);
  or or_17 (or_17_out, or_7_out, and_38_out);
  or or_18 (or_18_out, and_39_out, and_40_out);
  or or_19 (c, or_8_out, or_9_out);
  or or_20 (or_20_out, or_10_out, and_41_out);
  or or_21 (or_21_out, and_42_out, and_43_out);
  or or_22 (or_22_out, or_12_out, and_44_out);
  or or_23 (or_23_out, and_45_out, and_46_out);
  or or_24 (g, or_13_out, or_14_out);
  or or_25 (a, or_15_out, or_16_out);
  or or_26 (b, or_17_out, or_18_out);
  or or_27 (d, or_20_out, or_21_out);
  or or_28 (f, or_22_out, or_23_out);

  // Notes on the sheet:
  //   2107007        2108008
  //   2107008
  //   2107007
endmodule

module combinational (
  input  m,
  input  w,
  input  x,
  input  y,
  input  z,
  output a,
  output b,
  output c,
  output d
);

  wire and_1_out, and_2_out, and_3_out, and_4_out, and_5_out, and_6_out, and_7_out, and_8_out, and_9_out,
       and_10_out, and_11_out, and_12_out, and_13_out, and_14_out, and_15_out, and_16_out, and_17_out,
       and_18_out, not_1_out, not_2_out, not_3_out, not_4_out, not_5_out, not_6_out, not_7_out, not_8_out,
       not_9_out, not_10_out, not_11_out, not_12_out, not_13_out, not_14_out, not_15_out, not_16_out,
       not_17_out, not_18_out, not_19_out, not_20_out, not_21_out, not_22_out;

  not not_1 (not_1_out, m);
  not not_2 (not_2_out, x);
  not not_3 (not_3_out, y);
  not not_4 (not_4_out, z);
  not not_5 (not_5_out, w);
  not not_6 (not_6_out, m);
  not not_7 (not_7_out, w);
  not not_8 (not_8_out, y);
  not not_9 (not_9_out, y);
  not not_10 (not_10_out, z);
  not not_11 (not_11_out, x);
  not not_12 (not_12_out, m);
  not not_13 (not_13_out, w);
  not not_14 (not_14_out, x);
  not not_15 (not_15_out, z);
  not not_16 (not_16_out, y);
  not not_17 (not_17_out, m);
  not not_18 (not_18_out, w);
  not not_19 (not_19_out, x);
  not not_20 (not_20_out, w);
  not not_21 (not_21_out, y);
  not not_22 (not_22_out, z);
  and and_1 (and_1_out, not_1_out, w);
  and and_2 (and_2_out, w, not_2_out);
  and and_3 (and_3_out, w, not_3_out);
  and and_4 (and_4_out, w, not_4_out);
  and and_5 (and_5_out, m, not_5_out, x, y, z);
  and and_6 (and_6_out, not_6_out, x);
  and and_7 (and_7_out, not_7_out, x, not_8_out);
  and and_8 (and_8_out, x, not_9_out, z);
  and and_9 (and_9_out, x, y, not_10_out);
  and and_10 (and_10_out, m, w, not_11_out, y, z);
  and and_11 (and_11_out, not_12_out, y);
  and and_12 (and_12_out, not_13_out, not_14_out, y);
  and and_13 (and_13_out, y, not_15_out);
  and and_14 (and_14_out, m, w, not_16_out, z);
  and and_15 (and_15_out, not_17_out, z);
  and and_16 (and_16_out, not_18_out, not_19_out, z);
  and and_17 (and_17_out, not_20_out, not_21_out, z);
  and and_18 (and_18_out, m, w, not_22_out);
  or or_1 (a, and_1_out, and_2_out, and_3_out, and_4_out, and_5_out);
  or or_2 (b, and_6_out, and_7_out, and_8_out, and_9_out, and_10_out);
  or or_3 (c, and_11_out, and_12_out, and_13_out, and_14_out);
  or or_4 (d, and_15_out, and_16_out, and_17_out, and_18_out);
endmodule

module combinationalh (
  input  m,
  input  w,
  input  x,
  input  y,
  input  z,
  output a,
  output b,
  output c,
  output d
);

  wire and_1_out, and_2_out, and_3_out, and_5_out, and_6_out, and_7_out, and_8_out, and_9_out, and_10_out,
       not_1_out, not_2_out, not_3_out, not_4_out, not_5_out, or_1_out, or_2_out;

  and and_1 (and_1_out, m, y);
  not not_1 (not_1_out, m);
  and and_2 (and_2_out, m, x);
  not not_2 (not_2_out, w);
  not not_3 (not_3_out, x);
  not not_4 (not_4_out, y);
  and and_3 (and_3_out, and_1_out, z);
  and and_4 (b, not_1_out, x);
  or or_1 (or_1_out, y, and_2_out);
  and and_5 (and_5_out, m, w);
  not not_5 (not_5_out, m);
  and and_6 (and_6_out, not_2_out, not_3_out);
  and and_7 (and_7_out, not_4_out, z);
  or or_2 (or_2_out, w, and_3_out);
  and and_8 (and_8_out, m, x);
  or or_3 (c, or_1_out, and_5_out);
  and and_9 (and_9_out, not_5_out, z);
  or or_4 (d, and_9_out, and_10_out);
  and and_10 (and_10_out, and_6_out, and_7_out);
  or or_5 (a, or_2_out, and_8_out);
endmodule

module counter10 (
  input  in_1,
  input  in_2,
  output D,
  output C,
  output B,
  output A
);

  wire and_1_out, clock_1_out;

  Clock clock_1 (.out(clock_1_out));
  J_K_Flip_Flop #(.trigger("falling")) j_k_ff_1 (
    .J(in_1), .clk(clock_1_out), .K(in_1), .Q(D), .preset(in_2), .reset(and_1_out));  // open: Qn, en
  J_K_Flip_Flop #(.trigger("falling")) j_k_ff_2 (
    .J(in_1), .clk(D), .K(in_1), .Q(C), .preset(in_2), .reset(and_1_out));  // open: Qn, en
  J_K_Flip_Flop #(.trigger("falling")) j_k_ff_3 (
    .J(in_1), .clk(C), .K(in_1), .Q(B), .preset(in_2), .reset(and_1_out));  // open: Qn, en
  J_K_Flip_Flop #(.trigger("falling")) j_k_ff_4 (
    .J(in_1), .clk(B), .K(in_1), .Q(A), .preset(in_2), .reset(and_1_out));  // open: Qn, en
  and and_1 (and_1_out, C, A);

  // Notes on the sheet:
  //   2107008
endmodule

module counter6 (
  input  in_1,
  input  in_2,
  output A,
  output C,
  output B
);

  wire and_1_out;

  J_K_Flip_Flop #(.trigger("falling")) j_k_ff_1 (
    .J(in_1), .K(in_1), .Q(C), .preset(in_2), .reset(and_1_out));  // open: clk, Qn, en
  J_K_Flip_Flop #(.trigger("falling")) j_k_ff_2 (
    .J(in_1), .clk(C), .K(in_1), .Q(B), .preset(in_2), .reset(and_1_out));  // open: Qn, en
  J_K_Flip_Flop #(.trigger("falling")) j_k_ff_3 (
    .J(in_1), .clk(B), .K(in_1), .Q(A), .preset(in_2), .reset(and_1_out));  // open: Qn, en
  and and_1 (and_1_out, B, A);
endmodule

module counter2 (
  input  in_1,
  input  in_2,
  output out_3
);

  J_K_Flip_Flop #(.trigger("falling")) j_k_ff_1 (
    .J(in_1), .K(in_1), .Q(out_3), .preset(in_2), .reset(in_2));  // open: clk, Qn, en

  // Notes on the sheet:
  //   2107008
endmodule

module MINMUTESCLOCK (
  input  _10in,
  input  _0in,
  input  _6in,
  input  clk,
  input  _10pre,
  input  _6pre,
  output A,
  output D,
  output C,
  output B,
  output C_2,
  output B_2,
  output A_2,
  output \tri ,
  output a_3,
  output b_3,
  output c_3,
  output B_4,
  output d_2,
  output C_4,
  output e,
  output D_3,
  output f,
  output E_2,
  output g,
  output F_2,
  output G_2
);

  wire and_2_out, and_3_out, and_4_out, and_5_out, and_6_out, and_7_out, and_8_out, and_9_out, and_10_out,
       and_11_out, and_12_out, and_13_out, and_14_out, and_15_out, and_16_out, and_17_out, and_18_out,
       and_19_out, and_20_out, and_21_out, and_22_out, and_23_out, and_24_out, and_25_out, and_26_out,
       and_27_out, and_28_out, and_29_out, and_30_out, and_31_out, and_32_out, and_33_out, and_34_out,
       and_35_out, and_36_out, and_37_out, and_38_out, and_39_out, and_40_out, and_41_out, and_42_out,
       and_43_out, and_44_out, and_45_out, and_46_out, and_47_out, and_48_out, and_49_out, and_50_out,
       and_51_out, and_52_out, and_53_out, and_54_out, and_55_out, and_56_out, and_57_out, and_58_out,
       and_59_out, and_60_out, and_61_out, and_62_out, and_63_out, and_64_out, and_65_out, and_66_out,
       and_67_out, and_68_out, and_69_out, and_70_out, j_k_ff_3_q, not_1_out, not_2_out, not_3_out,
       not_4_out, not_5_out, not_6_out, not_7_out, not_8_out, not_9_out, not_10_out, not_11_out, not_12_out,
       not_13_out, not_14_out, not_15_out, not_16_out, not_17_out, not_18_out, not_19_out, not_20_out,
       not_21_out, not_22_out, not_23_out, not_24_out, not_25_out, not_26_out, not_27_out, not_28_out,
       not_29_out, not_30_out, not_31_out, not_32_out, not_33_out, not_34_out, not_35_out, not_36_out,
       not_37_out, not_38_out, not_39_out, not_40_out, not_41_out, not_42_out, not_43_out, not_44_out,
       not_45_out, not_46_out, not_47_out, not_48_out, not_49_out, not_50_out, not_51_out, not_52_out,
       not_53_out, not_54_out, not_55_out, not_56_out, not_57_out, not_58_out, not_59_out, not_60_out,
       not_61_out, not_62_out, not_63_out, not_64_out, not_65_out, not_66_out, not_67_out, not_68_out,
       not_69_out, not_70_out, not_71_out, not_72_out, not_73_out, not_74_out, not_75_out, or_1_out,
       or_9_out, or_10_out, or_11_out, or_12_out, or_13_out, or_14_out, or_15_out, or_16_out, or_17_out,
       or_18_out, or_19_out, or_21_out, or_22_out, or_23_out, or_24_out, or_25_out, or_26_out, or_27_out,
       or_29_out, or_30_out, or_31_out, or_32_out;

  J_K_Flip_Flop #(.trigger("falling")) j_k_ff_1 (
    .J(_6in), .clk(or_9_out), .K(_6in), .Q(C_2), .preset(_6pre), .reset(\tri ));  // open: Qn, en
  or or_1 (or_1_out, C_2, B_2, j_k_ff_3_q);
  J_K_Flip_Flop #(.trigger("falling")) j_k_ff_2 (
    .J(_6in), .clk(C_2), .K(_6in), .Q(B_2), .preset(_6pre), .reset(\tri ));  // open: Qn, en
  J_K_Flip_Flop #(.trigger("falling")) j_k_ff_3 (
    .J(_6in), .clk(B_2), .K(_6in), .Q(j_k_ff_3_q), .preset(_6pre), .reset(\tri ));  // open: Qn, en
  and and_1 (\tri , B_2, j_k_ff_3_q);
  J_K_Flip_Flop #(.trigger("falling")) j_k_ff_4 (
    .J(_10in), .clk(clk), .K(_10in), .Q(D), .preset(_10pre), .reset(or_9_out));  // open: Qn, en
  J_K_Flip_Flop #(.trigger("falling")) j_k_ff_5 (
    .J(_10in), .clk(D), .K(_10in), .Q(C), .preset(_10pre), .reset(or_9_out));  // open: Qn, en
  J_K_Flip_Flop #(.trigger("falling")) j_k_ff_6 (
    .J(_10in), .clk(C), .K(_10in), .Q(B), .preset(_10pre), .reset(or_9_out));  // open: Qn, en
  not not_1 (not_1_out, B);
  not not_2 (not_2_out, D);
  not not_3 (not_3_out, C);
  not not_4 (not_4_out, D);
  not not_5 (not_5_out, C);
  not not_6 (not_6_out, B);
  not not_7 (not_7_out, D);
  not not_8 (not_8_out, or_1_out);
  not not_9 (not_9_out, B);
  not not_10 (not_10_out, D);
  not not_11 (not_11_out, C);
  not not_12 (not_12_out, A);
  not not_13 (not_13_out, B);
  not not_14 (not_14_out, D);
  not not_15 (not_15_out, D);
  not not_16 (not_16_out, or_1_out);
  not not_17 (not_17_out, B);
  not not_18 (not_18_out, D);
  not not_19 (not_19_out, C);
  not not_20 (not_20_out, D);
  not not_21 (not_21_out, or_1_out);
  not not_22 (not_22_out, C);
  not not_23 (not_23_out, D);
  not not_24 (not_24_out, B);
  not not_25 (not_25_out, or_1_out);
  not not_26 (not_26_out, C);
  not not_27 (not_27_out, D);
  and and_2 (and_2_out, not_1_out, not_2_out);
  and and_3 (and_3_out, B, D);
  not not_28 (not_28_out, B);
  and and_4 (and_4_out, not_3_out, not_4_out);
  or or_2 (b_3, not_28_out, and_4_out, and_5_out);
  and and_5 (and_5_out, C, D);
  or or_3 (c_3, not_5_out, D, B);
  and and_6 (and_6_out, not_6_out, not_7_out);
  and and_7 (and_7_out, not_8_out, C);
  and and_8 (and_8_out, not_9_out, C);
  and and_9 (and_9_out, C, not_10_out);
  and and_10 (and_10_out, B, not_11_out, D);
  and and_11 (and_11_out, not_12_out, not_13_out, not_14_out);
  and and_12 (and_12_out, C, not_15_out);
  and and_13 (and_13_out, not_16_out, B, C);
  and and_14 (and_14_out, or_1_out, not_17_out, not_18_out);
  and and_15 (and_15_out, not_19_out, not_20_out);
  and and_16 (and_16_out, not_21_out, B);
  and and_17 (and_17_out, B, not_22_out);
  and and_18 (and_18_out, B, not_23_out);
  and and_19 (and_19_out, not_24_out, C);
  and and_20 (and_20_out, not_25_out, B);
  and and_21 (and_21_out, B, not_26_out);
  and and_22 (and_22_out, B, not_27_out);
  J_K_Flip_Flop #(.trigger("falling")) j_k_ff_7 (
    .J(_10in), .clk(B), .K(_10in), .Q(A), .preset(_10pre), .reset(or_9_out));  // open: Qn, en
  or or_4 (a_3, and_2_out, C, and_3_out, A);
  or or_5 (d_2, and_6_out, and_7_out, and_8_out, and_9_out, and_10_out, A);
  or or_6 (e, and_11_out, and_12_out, and_13_out, and_14_out);
  or or_7 (f, and_15_out, and_16_out, and_17_out, and_18_out, A);
  or or_8 (g, and_19_out, and_20_out, and_21_out, and_22_out, A);
  not not_29 (not_29_out, C);
  not not_30 (not_30_out, B);
  not not_31 (not_31_out, or_1_out);
  and and_23 (and_23_out, D, not_29_out, not_30_out, A, not_31_out);
  not not_32 (not_32_out, D);
  and and_24 (and_24_out, not_32_out, C, not_30_out, A, or_1_out);
  or or_9 (or_9_out, and_23_out, and_24_out);
  not not_33 (not_33_out, j_k_ff_3_q);
  not not_34 (not_34_out, _0in);
  not not_35 (not_35_out, B_2);
  not not_36 (not_36_out, _0in);
  not not_37 (not_37_out, B_2);
  not not_38 (not_38_out, _0in);
  not not_39 (not_39_out, _0in);
  not not_40 (not_40_out, j_k_ff_3_q);
  not not_41 (not_41_out, j_k_ff_3_q);
  not not_42 (not_42_out, j_k_ff_3_q);
  not not_43 (not_43_out, C_2);
  not not_44 (not_44_out, C_2);
  not not_45 (not_45_out, _0in);
  not not_46 (not_46_out, j_k_ff_3_q);
  not not_47 (not_47_out, C_2);
  not not_48 (not_48_out, _0in);
  not not_49 (not_49_out, j_k_ff_3_q);
  not not_50 (not_50_out, C_2);
  not not_51 (not_51_out, _0in);
  not not_52 (not_52_out, _0in);
  and and_25 (and_25_out, _0in, not_33_out);
  not not_53 (not_53_out, B_2);
  not not_54 (not_54_out, _0in);
  not not_55 (not_55_out, j_k_ff_3_q);
  and and_26 (and_26_out, not_34_out, not_35_out);
  not not_56 (not_56_out, C_2);
  not not_57 (not_57_out, _0in);
  not not_58 (not_58_out, B_2);
  and and_27 (and_27_out, not_36_out, not_37_out);
  and and_28 (and_28_out, not_38_out, C_2);
  not not_59 (not_59_out, B_2);
  not not_60 (not_60_out, _0in);
  not not_61 (not_61_out, j_k_ff_3_q);
  and and_29 (and_29_out, not_39_out, not_40_out);
  not not_62 (not_62_out, C_2);
  and and_30 (and_30_out, not_41_out, B_2);
  not not_63 (not_63_out, B_2);
  and and_31 (and_31_out, not_42_out, not_43_out);
  and and_32 (and_32_out, B_2, not_44_out);
  and and_33 (and_33_out, _0in, B_2);
  and and_34 (and_34_out, _0in, j_k_ff_3_q);
  not not_64 (not_64_out, B_2);
  not not_65 (not_65_out, C_2);
  and and_35 (and_35_out, not_45_out, j_k_ff_3_q);
  not not_66 (not_66_out, B_2);
  and and_36 (and_36_out, not_46_out, B_2);
  and and_37 (and_37_out, B_2, not_47_out);
  and and_38 (and_38_out, not_48_out, j_k_ff_3_q);
  not not_67 (not_67_out, B_2);
  not not_68 (not_68_out, j_k_ff_3_q);
  and and_39 (and_39_out, not_49_out, not_50_out);
  and and_40 (and_40_out, not_51_out, B_2);
  and and_41 (and_41_out, not_52_out, j_k_ff_3_q);
  and and_42 (and_42_out, j_k_ff_3_q, B_2);
  and and_43 (and_43_out, and_25_out, not_53_out);
  not not_69 (not_69_out, C_2);
  and and_44 (and_44_out, not_54_out, not_55_out);
  and and_45 (and_45_out, and_26_out, not_56_out);
  not not_70 (not_70_out, j_k_ff_3_q);
  not not_71 (not_71_out, C_2);
  and and_46 (and_46_out, not_57_out, B_2);
  and and_47 (and_47_out, _0in, not_58_out);
  or or_10 (or_10_out, and_27_out, and_28_out);
  and and_48 (and_48_out, not_59_out, C_2);
  and and_49 (and_49_out, not_60_out, j_k_ff_3_q);
  and and_50 (and_50_out, _0in, not_61_out);
  and and_51 (and_51_out, and_29_out, not_62_out);
  and and_52 (and_52_out, and_30_out, C_2);
  and and_53 (and_53_out, j_k_ff_3_q, not_63_out);
  and and_54 (and_54_out, j_k_ff_3_q, B_2);
  not not_72 (not_72_out, C_2);
  not not_73 (not_73_out, B_2);
  or or_11 (or_11_out, and_31_out, and_32_out);
  or or_12 (or_12_out, and_33_out, and_34_out);
  and and_55 (and_55_out, not_64_out, not_65_out);
  and and_56 (and_56_out, and_35_out, not_66_out);
  not not_74 (not_74_out, C_2);
  not not_75 (not_75_out, j_k_ff_3_q);
  or or_13 (or_13_out, and_36_out, and_37_out);
  and and_57 (and_57_out, and_38_out, not_67_out);
  and and_58 (and_58_out, _0in, not_68_out);
  and and_59 (and_59_out, _0in, C_2);
  or or_14 (or_14_out, and_39_out, and_40_out);
  and and_60 (and_60_out, and_41_out, C_2);
  or or_15 (or_15_out, and_42_out, and_43_out);
  and and_61 (and_61_out, _0in, not_69_out);
  or or_16 (or_16_out, and_44_out, and_45_out);
  and and_62 (and_62_out, not_70_out, not_71_out);
  and and_63 (and_63_out, and_46_out, C_2);
  and and_64 (and_64_out, and_47_out, C_2);
  or or_17 (or_17_out, or_10_out, and_48_out);
  or or_18 (or_18_out, and_49_out, and_50_out);
  or or_19 (or_19_out, and_51_out, and_52_out);
  and and_65 (and_65_out, and_53_out, C_2);
  and and_66 (and_66_out, and_54_out, not_72_out);
  and and_67 (and_67_out, _0in, not_73_out);
  or or_20 (E_2, or_11_out, or_12_out);
  or or_21 (or_21_out, and_55_out, and_56_out);
  and and_68 (and_68_out, j_k_ff_3_q, not_74_out);
  and and_69 (and_69_out, _0in, not_75_out);
  and and_70 (and_70_out, _0in, B_2);
  or or_22 (or_22_out, or_13_out, and_57_out);
  or or_23 (or_23_out, and_58_out, and_59_out);
  or or_24 (or_24_out, or_14_out, and_60_out);
  or or_25 (or_25_out, or_15_out, and_61_out);
  or or_26 (or_26_out, or_16_out, and_62_out);
  or or_27 (or_27_out, and_63_out, and_64_out);
  or or_28 (C_4, or_17_out, or_18_out);
  or or_29 (or_29_out, or_19_out, and_65_out);
  or or_30 (or_30_out, and_66_out, and_67_out);
  or or_31 (or_31_out, or_21_out, and_68_out);
  or or_32 (or_32_out, and_69_out, and_70_out);
  or or_33 (G_2, or_22_out, or_23_out);
  or or_34 (A_2, or_24_out, or_25_out);
  or or_35 (B_4, or_26_out, or_27_out);
  or or_36 (D_3, or_29_out, or_30_out);
  or or_37 (F_2, or_31_out, or_32_out);

  // Notes on the sheet:
  //   2107008
  //   2107007
endmodule

module counter60 (
  input  in_1,
  input  in_2,
  input  in_3,
  input  in_4,
  input  w,
  output A,
  output D,
  output C,
  output B,
  output A_2,
  output C_2,
  output B_2
);

  wire and_1_out, and_2_out, and_3_out, and_4_out, and_5_out, and_6_out, and_7_out, and_8_out, and_9_out,
       and_10_out, and_11_out, and_12_out, and_13_out, and_14_out, and_15_out, and_16_out, and_17_out,
       and_18_out, and_19_out, and_20_out, and_21_out, and_22_out, and_23_out, and_24_out, and_25_out,
       and_26_out, and_27_out, and_28_out, and_29_out, and_30_out, and_31_out, and_32_out, and_33_out,
       and_34_out, and_35_out, and_36_out, and_37_out, and_38_out, and_39_out, and_40_out, and_41_out,
       and_42_out, and_43_out, and_44_out, and_45_out, and_46_out, and_47_out, and_48_out, and_49_out,
       and_50_out, and_51_out, and_52_out, and_53_out, and_54_out, and_55_out, and_56_out, and_57_out,
       and_58_out, and_59_out, and_60_out, and_61_out, and_62_out, and_63_out, and_64_out, and_65_out,
       and_66_out, and_67_out, and_68_out, and_69_out, and_70_out, and_71_out, and_72_out, and_73_out,
       and_74_out, and_75_out, and_76_out, and_77_out, and_78_out, and_79_out, and_80_out, and_81_out,
       and_82_out, and_83_out, and_84_out, and_85_out, and_86_out, and_87_out, and_88_out, and_89_out,
       and_90_out, and_91_out, and_92_out, and_93_out, and_94_out, clock_1_out, not_1_out, not_2_out,
       not_3_out, not_4_out, not_5_out, not_6_out, not_7_out, not_8_out, not_9_out, not_10_out, not_11_out,
       not_12_out, not_13_out, not_14_out, not_15_out, not_16_out, not_17_out, not_18_out, not_19_out,
       not_20_out, not_21_out, not_22_out, not_23_out, not_24_out, not_25_out, not_26_out, not_27_out,
       not_28_out, not_29_out, not_30_out, not_31_out, not_32_out, not_33_out, not_34_out, not_35_out,
       not_36_out, not_37_out, not_38_out, not_39_out, not_40_out, not_41_out, not_42_out, not_43_out,
       not_44_out, not_45_out, not_46_out, not_47_out, not_48_out, not_49_out, not_50_out, not_51_out,
       not_52_out, not_53_out, not_54_out, not_55_out, not_56_out, not_57_out, not_58_out, not_59_out,
       not_60_out, not_61_out, not_62_out, not_63_out, not_64_out, not_65_out, not_66_out, not_67_out,
       not_68_out, not_69_out, not_70_out, not_71_out, not_72_out, not_73_out, not_74_out, not_75_out,
       not_76_out, not_77_out, not_78_out, not_79_out, not_80_out, not_81_out, not_82_out, not_83_out,
       not_84_out, not_85_out, not_86_out, or_1_out, or_2_out, or_3_out, or_4_out, or_5_out, or_6_out,
       or_7_out, or_8_out, or_9_out, or_10_out, or_11_out, or_12_out, or_13_out, or_14_out, or_15_out,
       or_16_out, or_17_out, or_18_out, or_19_out, or_20_out, or_21_out, or_22_out, or_23_out, or_24_out,
       or_25_out, or_26_out, or_27_out, or_28_out, or_29_out, or_30_out, or_31_out, or_32_out, or_33_out,
       or_34_out, or_35_out, or_36_out, or_37_out, or_38_out, or_39_out, or_40_out, or_41_out, or_42_out,
       or_43_out, or_44_out, or_45_out, or_46_out, or_47_out, or_48_out, or_49_out, or_50_out, or_51_out,
       or_52_out, or_53_out, or_54_out, or_55_out, or_56_out, undriven, undriven_2;

  J_K_Flip_Flop #(.trigger("falling")) j_k_ff_1 (
    .J(in_1), .clk(and_48_out), .K(in_1), .Q(C_2), .preset(in_4), .reset(and_1_out));  // open: Qn, en
  J_K_Flip_Flop #(.trigger("falling")) j_k_ff_2 (
    .J(in_1), .clk(C_2), .K(in_1), .Q(B_2), .preset(in_4), .reset(and_1_out));  // open: Qn, en
  not not_1 (not_1_out, A);
  not not_2 (not_2_out, w);
  not not_3 (not_3_out, B_2);
  not not_4 (not_4_out, w);
  not not_5 (not_5_out, B_2);
  not not_6 (not_6_out, w);
  not not_7 (not_7_out, w);
  not not_8 (not_8_out, A);
  not not_9 (not_9_out, A);
  not not_10 (not_10_out, A);
  not not_11 (not_11_out, C_2);
  not not_12 (not_12_out, C_2);
  not not_13 (not_13_out, w);
  not not_14 (not_14_out, A);
  not not_15 (not_15_out, C_2);
  not not_16 (not_16_out, w);
  J_K_Flip_Flop #(.trigger("falling")) j_k_ff_3 (
    .J(in_1), .clk(B_2), .K(in_1), .Q(A), .preset(in_4), .reset(and_1_out));  // open: Qn, en
  and and_1 (and_1_out, B_2, A);
  not not_17 (not_17_out, A);
  not not_18 (not_18_out, C_2);
  not not_19 (not_19_out, w);
  not not_20 (not_20_out, w);
  and and_2 (and_2_out, w, not_1_out);
  not not_21 (not_21_out, B_2);
  not not_22 (not_22_out, w);
  not not_23 (not_23_out, A);
  and and_3 (and_3_out, not_2_out, not_3_out);
  not not_24 (not_24_out, C_2);
  not not_25 (not_25_out, w);
  not not_26 (not_26_out, B_2);
  and and_4 (and_4_out, not_4_out, not_5_out);
  and and_5 (and_5_out, not_6_out, C_2);
  not not_27 (not_27_out, B_2);
  not not_28 (not_28_out, w);
  not not_29 (not_29_out, A);
  and and_6 (and_6_out, not_7_out, not_8_out);
  not not_30 (not_30_out, C_2);
  and and_7 (and_7_out, not_9_out, B_2);
  not not_31 (not_31_out, B_2);
  and and_8 (and_8_out, not_10_out, not_11_out);
  and and_9 (and_9_out, B_2, not_12_out);
  and and_10 (and_10_out, w, B_2);
  and and_11 (and_11_out, w, A);
  not not_32 (not_32_out, B_2);
  not not_33 (not_33_out, C_2);
  and and_12 (and_12_out, not_13_out, A);
  not not_34 (not_34_out, B_2);
  and and_13 (and_13_out, not_14_out, B_2);
  and and_14 (and_14_out, B_2, not_15_out);
  and and_15 (and_15_out, not_16_out, A);
  not not_35 (not_35_out, B_2);
  not not_36 (not_36_out, A);
  and and_16 (and_16_out, not_17_out, not_18_out);
  and and_17 (and_17_out, not_19_out, B_2);
  and and_18 (and_18_out, not_20_out, A);
  and and_19 (and_19_out, A, B_2);
  and and_20 (and_20_out, and_2_out, not_21_out);
  not not_37 (not_37_out, C_2);
  and and_21 (and_21_out, not_22_out, not_23_out);
  and and_22 (and_22_out, and_3_out, not_24_out);
  not not_38 (not_38_out, A);
  not not_39 (not_39_out, C_2);
  and and_23 (and_23_out, not_25_out, B_2);
  and and_24 (and_24_out, w, not_26_out);
  or or_1 (or_1_out, and_4_out, and_5_out);
  and and_25 (and_25_out, not_27_out, C_2);
  and and_26 (and_26_out, not_28_out, A);
  and and_27 (and_27_out, w, not_29_out);
  and and_28 (and_28_out, and_6_out, not_30_out);
  and and_29 (and_29_out, and_7_out, C_2);
  and and_30 (and_30_out, A, not_31_out);
  and and_31 (and_31_out, A, B_2);
  not not_40 (not_40_out, C_2);
  not not_41 (not_41_out, B_2);
  or or_2 (or_2_out, and_8_out, and_9_out);
  or or_3 (or_3_out, and_10_out, and_11_out);
  and and_32 (and_32_out, not_32_out, not_33_out);
  and and_33 (and_33_out, and_12_out, not_34_out);
  not not_42 (not_42_out, C_2);
  not not_43 (not_43_out, A);
  or or_4 (or_4_out, and_13_out, and_14_out);
  and and_34 (and_34_out, and_15_out, not_35_out);
  and and_35 (and_35_out, w, not_36_out);
  and and_36 (and_36_out, w, C_2);
  or or_5 (or_5_out, and_16_out, and_17_out);
  and and_37 (and_37_out, and_18_out, C_2);
  or or_6 (or_6_out, and_19_out, and_20_out);
  and and_38 (and_38_out, w, not_37_out);
  or or_7 (or_7_out, and_21_out, and_22_out);
  and and_39 (and_39_out, not_38_out, not_39_out);
  and and_40 (and_40_out, and_23_out, C_2);
  and and_41 (and_41_out, and_24_out, C_2);
  or or_8 (or_8_out, or_1_out, and_25_out);
  or or_9 (or_9_out, and_26_out, and_27_out);
  or or_10 (or_10_out, and_28_out, and_29_out);
  and and_42 (and_42_out, and_30_out, C_2);
  and and_43 (and_43_out, and_31_out, not_40_out);
  and and_44 (and_44_out, w, not_41_out);
  or or_11 (or_11_out, or_2_out, or_3_out);
  or or_12 (or_12_out, and_32_out, and_33_out);
  and and_45 (and_45_out, A, not_42_out);
  and and_46 (and_46_out, w, not_43_out);
  and and_47 (and_47_out, w, B_2);
  or or_13 (or_13_out, or_4_out, and_34_out);
  or or_14 (or_14_out, and_35_out, and_36_out);
  or or_15 (or_15_out, or_5_out, and_37_out);
  or or_16 (or_16_out, or_6_out, and_38_out);
  or or_17 (or_17_out, or_7_out, and_39_out);
  or or_18 (or_18_out, and_40_out, and_41_out);
  or or_19 (or_19_out, or_8_out, or_9_out);
  or or_20 (or_20_out, or_10_out, and_42_out);
  or or_21 (or_21_out, and_43_out, and_44_out);
  or or_22 (or_22_out, or_12_out, and_45_out);
  or or_23 (or_23_out, and_46_out, and_47_out);
  or or_24 (or_24_out, or_13_out, or_14_out);
  Clock clock_1 (.out(clock_1_out));
  or or_25 (or_25_out, or_15_out, or_16_out);
  or or_26 (or_26_out, or_17_out, or_18_out);
  or or_27 (or_27_out, or_20_out, or_21_out);
  or or_28 (or_28_out, or_22_out, or_23_out);
  J_K_Flip_Flop #(.trigger("falling")) j_k_ff_4 (
    .J(in_2), .clk(clock_1_out), .K(in_2), .Q(D), .preset(in_3), .reset(and_48_out));  // open: Qn, en
  J_K_Flip_Flop #(.trigger("falling")) j_k_ff_5 (
    .J(in_2), .clk(D), .K(in_2), .Q(C), .preset(in_3), .reset(and_48_out));  // open: Qn, en
  _7_Segment_Display u_7_segment_display_1 (
    .g(or_24_out), .f(or_28_out), .a(or_25_out), .b(or_26_out), .e(or_11_out), .d(or_27_out), .c(or_19_out),
    .dp(undriven));
  J_K_Flip_Flop #(.trigger("falling")) j_k_ff_6 (
    .J(in_2), .clk(C), .K(in_2), .Q(B), .preset(in_3), .reset(and_48_out));  // open: Qn, en
  and and_48 (and_48_out, C, A_2);
  J_K_Flip_Flop #(.trigger("falling")) j_k_ff_7 (
    .J(in_2), .clk(B), .K(in_2), .Q(A_2), .preset(in_3), .reset(and_48_out));  // open: Qn, en
  not not_44 (not_44_out, B);
  not not_45 (not_45_out, D);
  not not_46 (not_46_out, A_2);
  not not_47 (not_47_out, A_2);
  and and_49 (and_49_out, A_2, not_48_out);
  not not_48 (not_48_out, B);
  not not_49 (not_49_out, C);
  not not_50 (not_50_out, A_2);
  not not_51 (not_51_out, B);
  not not_52 (not_52_out, A_2);
  and and_50 (and_50_out, not_52_out, not_53_out);
  not not_53 (not_53_out, C);
  not not_54 (not_54_out, D);
  not not_55 (not_55_out, A_2);
  not not_56 (not_56_out, C);
  not not_57 (not_57_out, A_2);
  and and_51 (and_51_out, not_57_out, not_58_out);
  not not_58 (not_58_out, C);
  not not_59 (not_59_out, A_2);
  and and_52 (and_52_out, not_59_out, D);
  not not_60 (not_60_out, C);
  not not_61 (not_61_out, A_2);
  not not_62 (not_62_out, B);
  not not_63 (not_63_out, A_2);
  and and_53 (and_53_out, not_63_out, not_64_out);
  not not_64 (not_64_out, B);
  not not_65 (not_65_out, D);
  not not_66 (not_66_out, B);
  and and_54 (and_54_out, not_66_out, C);
  not not_67 (not_67_out, C);
  not not_68 (not_68_out, B);
  and and_55 (and_55_out, not_68_out, not_69_out);
  not not_69 (not_69_out, D);
  and and_56 (and_56_out, C, not_70_out);
  not not_70 (not_70_out, D);
  and and_57 (and_57_out, A_2, C);
  and and_58 (and_58_out, A_2, B);
  not not_71 (not_71_out, C);
  not not_72 (not_72_out, D);
  not not_73 (not_73_out, A_2);
  and and_59 (and_59_out, not_73_out, B);
  not not_74 (not_74_out, C);
  not not_75 (not_75_out, B);
  and and_60 (and_60_out, not_75_out, C);
  and and_61 (and_61_out, C, not_76_out);
  not not_76 (not_76_out, D);
  not not_77 (not_77_out, A_2);
  and and_62 (and_62_out, not_77_out, B);
  not not_78 (not_78_out, C);
  not not_79 (not_79_out, B);
  and and_63 (and_63_out, not_44_out, not_45_out);
  and and_64 (and_64_out, not_46_out, C);
  and and_65 (and_65_out, not_47_out, B);
  and and_66 (and_66_out, B, C);
  and and_67 (and_67_out, and_49_out, not_49_out);
  not not_80 (not_80_out, D);
  and and_68 (and_68_out, not_50_out, not_51_out);
  and and_69 (and_69_out, and_50_out, not_54_out);
  not not_81 (not_81_out, B);
  not not_82 (not_82_out, D);
  and and_70 (and_70_out, not_55_out, C);
  and and_71 (and_71_out, A_2, not_56_out);
  or or_29 (or_29_out, and_51_out, and_52_out);
  and and_72 (and_72_out, not_60_out, D);
  and and_73 (and_73_out, not_61_out, B);
  and and_74 (and_74_out, A_2, not_62_out);
  and and_75 (and_75_out, and_53_out, not_65_out);
  and and_76 (and_76_out, and_54_out, D);
  and and_77 (and_77_out, B, not_67_out);
  and and_78 (and_78_out, B, C);
  not not_83 (not_83_out, D);
  not not_84 (not_84_out, C);
  or or_30 (or_30_out, and_55_out, and_56_out);
  or or_31 (or_31_out, and_57_out, and_58_out);
  and and_79 (and_79_out, not_71_out, not_72_out);
  and and_80 (and_80_out, and_59_out, not_74_out);
  not not_85 (not_85_out, D);
  not not_86 (not_86_out, B);
  or or_32 (or_32_out, and_60_out, and_61_out);
  and and_81 (and_81_out, and_62_out, not_78_out);
  and and_82 (and_82_out, A_2, not_79_out);
  and and_83 (and_83_out, A_2, D);
  or or_33 (or_33_out, and_63_out, and_64_out);
  and and_84 (and_84_out, and_65_out, D);
  or or_34 (or_34_out, and_66_out, and_67_out);
  and and_85 (and_85_out, A_2, not_80_out);
  or or_35 (or_35_out, and_68_out, and_69_out);
  and and_86 (and_86_out, not_81_out, not_82_out);
  and and_87 (and_87_out, and_70_out, D);
  and and_88 (and_88_out, and_71_out, D);
  or or_36 (or_36_out, or_29_out, and_72_out);
  or or_37 (or_37_out, and_73_out, and_74_out);
  or or_38 (or_38_out, and_75_out, and_76_out);
  and and_89 (and_89_out, and_77_out, D);
  and and_90 (and_90_out, and_78_out, not_83_out);
  and and_91 (and_91_out, A_2, not_84_out);
  or or_39 (or_39_out, or_30_out, or_31_out);
  or or_40 (or_40_out, and_79_out, and_80_out);
  and and_92 (and_92_out, B, not_85_out);
  and and_93 (and_93_out, A_2, not_86_out);
  and and_94 (and_94_out, A_2, C);
  or or_41 (or_41_out, or_32_out, and_81_out);
  or or_42 (or_42_out, and_82_out, and_83_out);
  or or_43 (or_43_out, or_33_out, and_84_out);
  or or_44 (or_44_out, or_34_out, and_85_out);
  or or_45 (or_45_out, or_35_out, and_86_out);
  or or_46 (or_46_out, and_87_out, and_88_out);
  or or_47 (or_47_out, or_36_out, or_37_out);
  or or_48 (or_48_out, or_38_out, and_89_out);
  or or_49 (or_49_out, and_90_out, and_91_out);
  or or_50 (or_50_out, or_40_out, and_92_out);
  or or_51 (or_51_out, and_93_out, and_94_out);
  or or_52 (or_52_out, or_41_out, or_42_out);
  or or_53 (or_53_out, or_43_out, or_44_out);
  or or_54 (or_54_out, or_45_out, or_46_out);
  or or_55 (or_55_out, or_48_out, or_49_out);
  or or_56 (or_56_out, or_50_out, or_51_out);
  _7_Segment_Display u_7_segment_display_2 (
    .g(or_52_out), .f(or_56_out), .a(or_53_out), .b(or_54_out), .e(or_39_out), .d(or_55_out), .c(or_47_out),
    .dp(undriven_2));

  // Notes on the sheet:
  //   2107008
  //   2107008
endmodule

module practise (
  input  in_1,
  input  in_2,
  input  in_3,
  input  in_4,
  input  in_5,
  output A,
  output D,
  output C,
  output B,
  output C_2,
  output B_2
);

  wire and_1_out, and_2_out, and_3_out, and_4_out, and_5_out, and_6_out, and_7_out, and_8_out, and_9_out,
       and_10_out, and_11_out, and_12_out, and_13_out, and_14_out, and_15_out, and_16_out, and_17_out,
       and_18_out, and_19_out, and_20_out, and_21_out, and_22_out, and_23_out, and_24_out, and_25_out,
       and_26_out, and_27_out, and_28_out, and_29_out, and_30_out, and_31_out, and_32_out, and_33_out,
       and_34_out, and_35_out, and_36_out, and_37_out, and_38_out, and_39_out, and_40_out, and_41_out,
       and_42_out, and_43_out, and_44_out, and_45_out, and_46_out, and_47_out, and_48_out, clock_1_out,
       j_k_ff_3_q, not_1_out, not_3_out, not_4_out, not_5_out, not_6_out, not_7_out, not_8_out, not_9_out,
       not_10_out, not_11_out, not_12_out, not_13_out, not_14_out, not_15_out, not_16_out, not_17_out,
       not_18_out, not_19_out, not_20_out, not_21_out, not_22_out, not_23_out, not_24_out, not_25_out,
       not_26_out, not_27_out, not_28_out, not_29_out, not_30_out, not_31_out, not_32_out, not_33_out,
       not_34_out, not_35_out, not_36_out, not_37_out, not_38_out, not_39_out, not_40_out, not_41_out,
       not_42_out, not_43_out, not_44_out, not_45_out, or_1_out, or_2_out, or_3_out, or_4_out, or_5_out,
       or_6_out, or_7_out, or_8_out, or_9_out, or_10_out, or_11_out, or_12_out, or_13_out, or_14_out,
       or_15_out, or_16_out, or_17_out, or_18_out, or_19_out, or_20_out, or_21_out, or_22_out, or_23_out,
       or_24_out, or_25_out, or_26_out, or_27_out, or_28_out, or_29_out, undriven, undriven_2, undriven_3,
       undriven_4, undriven_5, undriven_6, undriven_7, undriven_8;

  J_K_Flip_Flop #(.trigger("falling")) j_k_ff_1 (
    .J(in_3), .clk(and_2_out), .K(in_3), .Q(C_2), .preset(in_5), .reset(and_1_out));  // open: Qn, en
  or or_1 (or_1_out, C_2, B_2, j_k_ff_3_q);
  J_K_Flip_Flop #(.trigger("falling")) j_k_ff_2 (
    .J(in_3), .clk(C_2), .K(in_3), .Q(B_2), .preset(in_5), .reset(and_1_out));  // open: Qn, en
  not not_1 (not_1_out, or_1_out);
  J_K_Flip_Flop #(.trigger("falling")) j_k_ff_3 (
    .J(in_3), .clk(B_2), .K(in_3), .Q(j_k_ff_3_q), .preset(in_5), .reset(and_1_out));  // open: Qn, en
  and and_1 (and_1_out, B_2, j_k_ff_3_q);
  Clock clock_1 (.out(clock_1_out));
  // NOT_Gate not_2 is placed but not wired
  J_K_Flip_Flop #(.trigger("falling")) j_k_ff_4 (
    .J(in_1), .clk(clock_1_out), .K(in_1), .Q(D), .preset(in_4), .reset(and_2_out));  // open: Qn, en
  J_K_Flip_Flop #(.trigger("falling")) j_k_ff_5 (
    .J(in_1), .clk(D), .K(in_1), .Q(C), .preset(in_4), .reset(and_2_out));  // open: Qn, en
  J_K_Flip_Flop #(.trigger("falling")) j_k_ff_6 (
    .J(in_1), .clk(C), .K(in_1), .Q(B), .preset(in_4), .reset(and_2_out));  // open: Qn, en
  J_K_Flip_Flop #(.trigger("falling")) j_k_ff_7 (
    .J(in_1), .clk(B), .K(in_1), .Q(A), .preset(in_4), .reset(and_2_out));  // open: Qn, en
  and and_2 (and_2_out, C, A);
  _7_Segment_Display u_7_segment_display_1 (
    .g(undriven), .f(undriven_3), .a(undriven_2), .b(undriven_7), .e(undriven_4), .d(undriven_5),
    .c(undriven_6), .dp(undriven_8));
  not not_3 (not_3_out, j_k_ff_3_q);
  not not_4 (not_4_out, in_2);
  not not_5 (not_5_out, B_2);
  not not_6 (not_6_out, in_2);
  not not_7 (not_7_out, B_2);
  not not_8 (not_8_out, in_2);
  not not_9 (not_9_out, in_2);
  not not_10 (not_10_out, j_k_ff_3_q);
  not not_11 (not_11_out, j_k_ff_3_q);
  not not_12 (not_12_out, j_k_ff_3_q);
  not not_13 (not_13_out, C_2);
  not not_14 (not_14_out, C_2);
  not not_15 (not_15_out, in_2);
  not not_16 (not_16_out, j_k_ff_3_q);
  not not_17 (not_17_out, C_2);
  not not_18 (not_18_out, in_2);
  not not_19 (not_19_out, j_k_ff_3_q);
  not not_20 (not_20_out, C_2);
  not not_21 (not_21_out, in_2);
  not not_22 (not_22_out, in_2);
  and and_3 (and_3_out, in_2, not_3_out);
  not not_23 (not_23_out, B_2);
  not not_24 (not_24_out, in_2);
  not not_25 (not_25_out, j_k_ff_3_q);
  and and_4 (and_4_out, not_4_out, not_5_out);
  not not_26 (not_26_out, C_2);
  not not_27 (not_27_out, in_2);
  not not_28 (not_28_out, B_2);
  and and_5 (and_5_out, not_6_out, not_7_out);
  and and_6 (and_6_out, not_8_out, C_2);
  not not_29 (not_29_out, B_2);
  not not_30 (not_30_out, in_2);
  not not_31 (not_31_out, j_k_ff_3_q);
  and and_7 (and_7_out, not_9_out, not_10_out);
  not not_32 (not_32_out, C_2);
  and and_8 (and_8_out, not_11_out, B_2);
  not not_33 (not_33_out, B_2);
  and and_9 (and_9_out, not_12_out, not_13_out);
  and and_10 (and_10_out, B_2, not_14_out);
  and and_11 (and_11_out, in_2, B_2);
  and and_12 (and_12_out, in_2, j_k_ff_3_q);
  not not_34 (not_34_out, B_2);
  not not_35 (not_35_out, C_2);
  and and_13 (and_13_out, not_15_out, j_k_ff_3_q);
  not not_36 (not_36_out, B_2);
  and and_14 (and_14_out, not_16_out, B_2);
  and and_15 (and_15_out, B_2, not_17_out);
  and and_16 (and_16_out, not_18_out, j_k_ff_3_q);
  not not_37 (not_37_out, B_2);
  not not_38 (not_38_out, j_k_ff_3_q);
  and and_17 (and_17_out, not_19_out, not_20_out);
  and and_18 (and_18_out, not_21_out, B_2);
  and and_19 (and_19_out, not_22_out, j_k_ff_3_q);
  and and_20 (and_20_out, j_k_ff_3_q, B_2);
  and and_21 (and_21_out, and_3_out, not_23_out);
  not not_39 (not_39_out, C_2);
  and and_22 (and_22_out, not_24_out, not_25_out);
  and and_23 (and_23_out, and_4_out, not_26_out);
  not not_40 (not_40_out, j_k_ff_3_q);
  not not_41 (not_41_out, C_2);
  and and_24 (and_24_out, not_27_out, B_2);
  and and_25 (and_25_out, in_2, not_28_out);
  or or_2 (or_2_out, and_5_out, and_6_out);
  and and_26 (and_26_out, not_29_out, C_2);
  and and_27 (and_27_out, not_30_out, j_k_ff_3_q);
  and and_28 (and_28_out, in_2, not_31_out);
  and and_29 (and_29_out, and_7_out, not_32_out);
  and and_30 (and_30_out, and_8_out, C_2);
  and and_31 (and_31_out, j_k_ff_3_q, not_33_out);
  and and_32 (and_32_out, j_k_ff_3_q, B_2);
  not not_42 (not_42_out, C_2);
  not not_43 (not_43_out, B_2);
  or or_3 (or_3_out, and_9_out, and_10_out);
  or or_4 (or_4_out, and_11_out, and_12_out);
  and and_33 (and_33_out, not_34_out, not_35_out);
  and and_34 (and_34_out, and_13_out, not_36_out);
  not not_44 (not_44_out, C_2);
  not not_45 (not_45_out, j_k_ff_3_q);
  or or_5 (or_5_out, and_14_out, and_15_out);
  and and_35 (and_35_out, and_16_out, not_37_out);
  and and_36 (and_36_out, in_2, not_38_out);
  and and_37 (and_37_out, in_2, C_2);
  or or_6 (or_6_out, and_17_out, and_18_out);
  and and_38 (and_38_out, and_19_out, C_2);
  or or_7 (or_7_out, and_20_out, and_21_out);
  and and_39 (and_39_out, in_2, not_39_out);
  or or_8 (or_8_out, and_22_out, and_23_out);
  and and_40 (and_40_out, not_40_out, not_41_out);
  and and_41 (and_41_out, and_24_out, C_2);
  and and_42 (and_42_out, and_25_out, C_2);
  or or_9 (or_9_out, or_2_out, and_26_out);
  or or_10 (or_10_out, and_27_out, and_28_out);
  or or_11 (or_11_out, and_29_out, and_30_out);
  and and_43 (and_43_out, and_31_out, C_2);
  and and_44 (and_44_out, and_32_out, not_42_out);
  and and_45 (and_45_out, in_2, not_43_out);
  or or_12 (or_12_out, or_3_out, or_4_out);
  or or_13 (or_13_out, and_33_out, and_34_out);
  and and_46 (and_46_out, j_k_ff_3_q, not_44_out);
  and and_47 (and_47_out, in_2, not_45_out);
  and and_48 (and_48_out, in_2, B_2);
  or or_14 (or_14_out, or_5_out, and_35_out);
  or or_15 (or_15_out, and_36_out, and_37_out);
  or or_16 (or_16_out, or_6_out, and_38_out);
  or or_17 (or_17_out, or_7_out, and_39_out);
  or or_18 (or_18_out, or_8_out, and_40_out);
  or or_19 (or_19_out, and_41_out, and_42_out);
  or or_20 (or_20_out, or_9_out, or_10_out);
  or or_21 (or_21_out, or_11_out, and_43_out);
  or or_22 (or_22_out, and_44_out, and_45_out);
  or or_23 (or_23_out, or_13_out, and_46_out);
  or or_24 (or_24_out, and_47_out, and_48_out);
  or or_25 (or_25_out, or_14_out, or_15_out);
  _7_Segment_Display u_7_segment_display_2 (
    .g(or_25_out), .f(or_29_out), .a(or_26_out), .b(or_27_out), .e(or_12_out), .d(or_28_out), .c(or_20_out));  // open: dp
  or or_26 (or_26_out, or_16_out, or_17_out);
  or or_27 (or_27_out, or_18_out, or_19_out);
  or or_28 (or_28_out, or_21_out, or_22_out);
  or or_29 (or_29_out, or_23_out, or_24_out);

  // Notes on the sheet:
  //   2107008
  //   2107008
endmodule

module combinational_sce (
  input  M,
  input  A,
  input  B,
  input  C,
  input  D,
  output a_2,
  output b_2,
  output c_2,
  output d_2,
  output e,
  output f,
  output g
);

  wire and_1_out, and_2_out, and_3_out, and_4_out, and_5_out, and_6_out, and_7_out, and_8_out, and_9_out,
       and_10_out, and_11_out, and_12_out, and_13_out, and_14_out, and_15_out, and_16_out, and_17_out,
       and_18_out, and_19_out, and_20_out, and_21_out, and_22_out, and_23_out, and_24_out, and_25_out,
       and_26_out, not_1_out, not_2_out, not_3_out, not_4_out, not_5_out, not_6_out, not_7_out, not_8_out,
       not_9_out, not_10_out, not_11_out, not_12_out, not_13_out, not_14_out, not_15_out, not_16_out,
       not_17_out, not_18_out, not_19_out, not_20_out, not_21_out, not_22_out, not_23_out, not_24_out,
       not_25_out, not_26_out, not_27_out, not_28_out, not_29_out, not_30_out, not_31_out, not_32_out,
       not_33_out, not_34_out, not_35_out, not_36_out, not_37_out;

  not not_1 (not_1_out, D);
  not not_2 (not_2_out, M);
  not not_3 (not_3_out, B);
  not not_4 (not_4_out, B);
  not not_5 (not_5_out, D);
  not not_6 (not_6_out, C);
  not not_7 (not_7_out, D);
  not not_8 (not_8_out, M);
  not not_9 (not_9_out, C);
  not not_10 (not_10_out, C);
  not not_11 (not_11_out, D);
  not not_12 (not_12_out, B);
  not not_13 (not_13_out, D);
  not not_14 (not_14_out, M);
  not not_15 (not_15_out, D);
  not not_16 (not_16_out, C);
  not not_17 (not_17_out, B);
  not not_18 (not_18_out, A);
  not not_19 (not_19_out, B);
  not not_20 (not_20_out, D);
  not not_21 (not_21_out, D);
  not not_22 (not_22_out, M);
  not not_23 (not_23_out, A);
  not not_24 (not_24_out, B);
  not not_25 (not_25_out, C);
  not not_26 (not_26_out, B);
  not not_27 (not_27_out, D);
  not not_28 (not_28_out, C);
  not not_29 (not_29_out, D);
  not not_30 (not_30_out, M);
  not not_31 (not_31_out, D);
  not not_32 (not_32_out, C);
  not not_33 (not_33_out, B);
  not not_34 (not_34_out, M);
  not not_35 (not_35_out, C);
  not not_36 (not_36_out, D);
  not not_37 (not_37_out, B);
  or or_1 (a_2, not_1_out, C, B, M);
  and and_1 (and_1_out, not_2_out, not_3_out);
  and and_2 (and_2_out, not_4_out, not_5_out);
  and and_3 (and_3_out, not_6_out, not_7_out);
  and and_4 (and_4_out, C, D);
  and and_5 (and_5_out, not_8_out, not_9_out);
  and and_6 (and_6_out, not_10_out, not_11_out);
  and and_7 (and_7_out, C, D);
  and and_8 (and_8_out, not_12_out, not_13_out);
  and and_9 (and_9_out, not_14_out, C);
  and and_10 (and_10_out, C, not_15_out);
  and and_11 (and_11_out, B, not_16_out, D);
  and and_12 (and_12_out, M, not_17_out);
  and and_13 (and_13_out, not_18_out, not_19_out, not_20_out);
  and and_14 (and_14_out, C, not_21_out);
  and and_15 (and_15_out, not_22_out, B, C);
  and and_16 (and_16_out, M, not_23_out, not_24_out, not_25_out);
  and and_17 (and_17_out, M, not_26_out, not_27_out);
  and and_18 (and_18_out, not_28_out, not_29_out);
  and and_19 (and_19_out, not_30_out, B);
  and and_20 (and_20_out, B, not_31_out);
  and and_21 (and_21_out, M, not_32_out);
  and and_22 (and_22_out, not_33_out, C);
  and and_23 (and_23_out, not_34_out, B);
  and and_24 (and_24_out, B, not_35_out);
  and and_25 (and_25_out, B, not_36_out);
  and and_26 (and_26_out, M, not_37_out, D);
  or or_2 (b_2, and_1_out, and_2_out, and_3_out, and_4_out, A);
  or or_3 (c_2, and_5_out, and_6_out, and_7_out, B, A);
  or or_4 (d_2, and_8_out, and_9_out, and_10_out, and_11_out, and_12_out);
  or or_5 (e, and_13_out, and_14_out, and_15_out, and_16_out, and_17_out);
  or or_6 (f, and_18_out, and_19_out, and_20_out, and_21_out);
  or or_7 (g, and_22_out, and_23_out, and_24_out, and_25_out, A, and_26_out);
endmodule

module c0mbinational_sec (
  input  M,
  input  A,
  input  B,
  input  C,
  input  D,
  output a_2,
  output b_2,
  output c_2,
  output d_2,
  output e,
  output f,
  output g
);

  wire and_1_out, and_2_out, and_3_out, and_4_out, and_5_out, and_6_out, and_7_out, and_8_out, and_9_out,
       and_10_out, and_11_out, and_12_out, and_13_out, and_14_out, and_15_out, and_16_out, and_17_out,
       and_18_out, and_19_out, and_20_out, and_21_out, not_1_out, not_2_out, not_3_out, not_4_out, not_5_out,
       not_6_out, not_7_out, not_8_out, not_9_out, not_10_out, not_11_out, not_12_out, not_13_out,
       not_14_out, not_15_out, not_16_out, not_17_out, not_18_out, not_19_out, not_20_out, not_21_out,
       not_22_out, not_23_out, not_24_out, not_25_out, not_26_out, not_27_out, not_28_out;

  not not_1 (not_1_out, B);
  not not_2 (not_2_out, D);
  not not_3 (not_3_out, C);
  not not_4 (not_4_out, D);
  not not_5 (not_5_out, C);
  not not_6 (not_6_out, B);
  not not_7 (not_7_out, D);
  not not_8 (not_8_out, M);
  not not_9 (not_9_out, B);
  not not_10 (not_10_out, D);
  not not_11 (not_11_out, C);
  not not_12 (not_12_out, A);
  not not_13 (not_13_out, B);
  not not_14 (not_14_out, D);
  not not_15 (not_15_out, D);
  not not_16 (not_16_out, M);
  not not_17 (not_17_out, B);
  not not_18 (not_18_out, D);
  not not_19 (not_19_out, C);
  not not_20 (not_20_out, D);
  not not_21 (not_21_out, M);
  not not_22 (not_22_out, C);
  not not_23 (not_23_out, D);
  not not_24 (not_24_out, B);
  not not_25 (not_25_out, M);
  not not_26 (not_26_out, C);
  not not_27 (not_27_out, D);
  and and_1 (and_1_out, not_1_out, not_2_out);
  and and_2 (and_2_out, B, D);
  not not_28 (not_28_out, B);
  and and_3 (and_3_out, not_3_out, not_4_out);
  and and_4 (and_4_out, C, D);
  or or_1 (c_2, not_5_out, D, B);
  and and_5 (and_5_out, not_6_out, not_7_out);
  and and_6 (and_6_out, not_8_out, C);
  and and_7 (and_7_out, not_9_out, C);
  and and_8 (and_8_out, C, not_10_out);
  and and_9 (and_9_out, B, not_11_out, D);
  and and_10 (and_10_out, not_12_out, not_13_out, not_14_out);
  and and_11 (and_11_out, C, not_15_out);
  and and_12 (and_12_out, not_16_out, B, C);
  and and_13 (and_13_out, M, not_17_out, not_18_out);
  and and_14 (and_14_out, not_19_out, not_20_out);
  and and_15 (and_15_out, not_21_out, B);
  and and_16 (and_16_out, B, not_22_out);
  and and_17 (and_17_out, B, not_23_out);
  and and_18 (and_18_out, not_24_out, C);
  and and_19 (and_19_out, not_25_out, B);
  and and_20 (and_20_out, B, not_26_out);
  and and_21 (and_21_out, B, not_27_out);
  or or_2 (a_2, and_1_out, C, and_2_out, A);
  or or_3 (b_2, not_28_out, and_3_out, and_4_out);
  or or_4 (d_2, and_5_out, and_6_out, and_7_out, and_8_out, and_9_out, A);
  or or_5 (e, and_10_out, and_11_out, and_12_out, and_13_out);
  or or_6 (f, and_14_out, and_15_out, and_16_out, and_17_out, A);
  or or_7 (g, and_18_out, and_19_out, and_20_out, and_21_out, A);
endmodule

module hourcombination (
  input  _10in,
  input  clk,
  input  _2in,
  input  _10pre,
  input  _2pre,
  output A,
  output D,
  output C,
  output B,
  output A_2,
  output B_2,
  output C_2,
  output out_13,
  output D_2,
  output E,
  output G,
  output F,
  output a_3,
  output b_3,
  output c_3,
  output d_3,
  output e_2,
  output f_2,
  output g_2
);

  wire and_1_out, and_2_out, not_1_out, not_2_out, not_3_out, not_4_out, or_1_out;

  J_K_Flip_Flop #(.trigger("falling")) j_k_ff_1 (
    .J(_2in), .clk(or_1_out), .K(_2in), .Q(out_13), .preset(_2pre), .reset(_2pre));  // open: Qn, en
  _2segmentdisplay u_2segmentdisplay_1 (.Aa(out_13), .A(A), .B(B_2), .C(C_2), .D(D_2), .E(E), .F(F), .G(G));
  J_K_Flip_Flop #(.trigger("falling")) j_k_ff_2 (
    .J(_10in), .clk(clk), .K(_10in), .Q(D), .preset(_10pre), .reset(or_1_out));  // open: Qn, en
  J_K_Flip_Flop #(.trigger("falling")) j_k_ff_3 (
    .J(_10in), .clk(D), .K(_10in), .Q(C), .preset(_10pre), .reset(or_1_out));  // open: Qn, en
  J_K_Flip_Flop #(.trigger("falling")) j_k_ff_4 (
    .J(_10in), .clk(C), .K(_10in), .Q(B), .preset(_10pre), .reset(or_1_out));  // open: Qn, en
  J_K_Flip_Flop #(.trigger("falling")) j_k_ff_5 (
    .J(_10in), .clk(B), .K(_10in), .Q(A_2), .preset(_10pre), .reset(or_1_out));  // open: Qn, en
  _7segment u_7segment_1 (.w(A_2), .x(B), .y(C), .z(D), .a(a_3), .b(b_3), .c(c_3), .d(d_3), .e(e_2), .f(f_2), .g(g_2));
  not not_1 (not_1_out, D);
  not not_2 (not_2_out, B);
  not not_3 (not_3_out, out_13);
  and and_1 (and_1_out, not_1_out, C, not_2_out, A_2, not_3_out);
  not not_4 (not_4_out, A_2);
  and and_2 (and_2_out, not_1_out, C, not_2_out, not_4_out, out_13);
  or or_1 (or_1_out, and_1_out, and_2_out);

  // Notes on the sheet:
  //   2107008   2107007
endmodule

module _2segmentdisplay (
  input  Aa,
  output A,
  output B,
  output C,
  output D,
  output E,
  output F,
  output G
);

  not not_1 (A, Aa);
  or or_1 (B, A, Aa);
  not not_2 (G, B);

  assign C = B;
  assign D = A;
  assign E = A;
  assign F = A;

  // Notes on the sheet:
  //   2107007
  //   2107008
endmodule
